# Fritzing sketch principal (saved by Fritzing 0.9.3b)
circuit board: 11.1043cm x 17.4313cm
breadboards: 1

parts:
  Rasp = Raspberry Pi Zero
  J10 = female pin header, 13 pins [form="♀ (female)"]
  J11 = female pin header, 12 pins [form="♀ (female)"]
  P4B = Power Jack [package=power_jack_slot]
  Part1 = 16-Channel 12-bit PCA9685 PWM/Servo Driver
  P4F = Power Jack [package=power_jack_slot]
  P4E = Power Jack [package=power_jack_slot]
  Not = PICAXE-14M [package=THT]  # not connected
  Flip_Flop = PICAXE-14M [package=THT]  # not connected
  P4F1 = Power Jack [package=power_jack_slot]
  P4F2 = Power Jack [package=power_jack_slot]
  U1 = RJ45 Jack [package=rj45-8]  # not connected

nets:
  N1: Rasp.pin_9, Rasp.pin_25, Rasp.pin_34, Rasp.pin_39, J10.pin13, J11.pin7, J11.pin8, P4B.GNDBREAK, Part1.GND, P4F1.GNDBREAK, P4F2.GNDBREAK
  N2: J11.pin1, J11.pin2, P4E.PWR
  N3: J11.pin3, J11.pin4, P4E.GNDBREAK
  N4: J11.pin5, J11.pin6, P4B.PWR
  N5: J11.pin9, J11.pin10, P4F.GNDBREAK
  N6: J11.pin11, J11.pin12, P4F.PWR
  N7: Part1.V+, P4F2.PWR
  N8: Part1.VCC, P4F1.PWR

custom parts:
  16-Channel 12-bit PCA9685 PWM/Servo Driver: The Adafruit 16-Channel 12-bit PWM/Servo Driver will drive up to 16 servos over I2C with only 2 pins. The on-board PCA9685 PWM controller will drive all 16 channels simultaneously with no additional processing overhead. What's more, you can chain up to 62 of them to control up to 992 servos - all with the same 2 pins
